# Fritzing sketch poc-setup (saved by Fritzing 0.9.3b)
breadboards: 1

parts:
  U1 = NodeMCU V1.0
  DS1 = DS18B20 1-Wire Temperature Sensor [part_number=DS18B20]
  part = Resistor [tolerance=±5% resistance=4.7k package=THT]

nets:
  N1: U1.D1, DS1.DQ, part.Pin_1
  3V3: U1.3V3, DS1.VDD, part.Pin_0
  GND: U1.GND, DS1.GND

custom parts:
  NodeMCU V1.0: ESP8266 based NodeMCU
